// Logisim project 4BitAdderCirc.circ as structural Verilog: 1 circuit, main circuit 4Bit Adder
// Adder-4Bit
module _4Bit_Adder (
  input  Cin,
  input  A0,
  input  B0,
  input  A1,
  input  B1,
  input  A2,
  input  B2,
  input  A3,
  input  B3,
  output S0,
  output S1,
  output S2,
  output S3,
  output C_out
);

  wire fulladder_1_c_out, fulladder_2_c_out, fulladder_3_c_out;

  FullAdder fulladder_1 (.A(Cin), .B(A0), .C_in(B0), .S_out(S0), .C_out(fulladder_1_c_out));
  FullAdder fulladder_2 (.A(fulladder_1_c_out), .B(A1), .C_in(B1), .S_out(S1), .C_out(fulladder_2_c_out));
  FullAdder fulladder_3 (.A(fulladder_2_c_out), .B(A2), .C_in(B2), .S_out(S2), .C_out(fulladder_3_c_out));
  FullAdder fulladder_4 (.A(fulladder_3_c_out), .B(A3), .C_in(B3), .S_out(S3), .C_out(C_out));
endmodule
