// Logisim project ALU.circ as structural Verilog: 2 circuits, main circuit Alu
// ALU
module Alu (
  input  in_1,
  input  in_2,
  input  in_3,
  input  in_4,
  input  in_5,
  input  in_6,
  input  in_7,
  input  in_8,
  input  in_9,
  input  in_10,
  input  in_11,
  input  in_12,
  output [7:0] out_13
);

  wire [4:0] n4bit_adder_1_s0;
  wire [7:0] and_1_b1, fullshifter_1_out_3, fullshiftright_1_out_3, move_1_out_2, multiplier_1_s0,
       mux_8x1_8bit_1_iout, mux_8x1_8bit_2_iout, negative_1_out_5, not_1_out_5, or_1_b1, subtractor_1_out_9,
       xor_1_b1;

  Move move_1 (.in_1({in_5, in_6, in_7, in_8}), .out_2(move_1_out_2));
  Negative negative_1 (
    .in_1(in_8), .in_2(in_7), .in_3(in_6), .in_4(in_5), .out_5(negative_1_out_5[0]),
    .out_6(negative_1_out_5[1]), .out_7(negative_1_out_5[2]), .out_8(negative_1_out_5[3]),
    .out_9(negative_1_out_5[4]), .out_10(negative_1_out_5[5]), .out_11(negative_1_out_5[6]),
    .out_12(negative_1_out_5[7]));
  _4Bit_Adder u_4bit_adder_1 (
    .Cin(1'b0), .A0(in_8), .B0(in_4), .A1(in_7), .B1(in_3), .A2(in_6), .B2(in_2), .A3(in_5), .B3(in_1),
    .S0(n4bit_adder_1_s0[0]), .S1(n4bit_adder_1_s0[1]), .S2(n4bit_adder_1_s0[2]), .S3(n4bit_adder_1_s0[3]),
    .C_out(n4bit_adder_1_s0[4]));
  MUX_8x1_8Bit mux_8x1_8bit_1 (
    .I3(multiplier_1_s0), .I4(subtractor_1_out_9), .I5({3'b000, n4bit_adder_1_s0}), .I6(negative_1_out_5),
    .I7(move_1_out_2), .Iout(mux_8x1_8bit_1_iout), .Sel({in_11, in_10, in_9}));  // open: I0, I1, I2
  Subtractor subtractor_1 (
    .A0(in_8), .A1(in_7), .A2(in_6), .A3(in_5), .B0(in_4), .B1(in_3), .B2(in_2), .B3(in_1),
    .out_9(subtractor_1_out_9[0]), .out_10(subtractor_1_out_9[1]), .out_11(subtractor_1_out_9[2]),
    .out_12(subtractor_1_out_9[3]), .out_13(subtractor_1_out_9[4]), .out_14(subtractor_1_out_9[5]),
    .out_15(subtractor_1_out_9[6]), .out_16(subtractor_1_out_9[7]));
  Multiplier multiplier_1 (
    .A0(in_8), .A1(in_7), .A2(in_6), .A3(in_5), .B0(in_4), .B1(in_3), .B2(in_2), .B3(in_1),
    .S0(multiplier_1_s0[0]), .S1(multiplier_1_s0[1]), .S2(multiplier_1_s0[2]), .S3(multiplier_1_s0[3]),
    .S4(multiplier_1_s0[4]), .S5(multiplier_1_s0[5]), .S6(multiplier_1_s0[6]), .S7(multiplier_1_s0[7]));
  MUX_2x1_8Bit mux_2x1_8bit_1 (.in_1(mux_8x1_8bit_2_iout), .in_2(mux_8x1_8bit_1_iout), .out_4(out_13), .in_3(in_12));
  NOT not_1 (
    .in_1(in_8), .in_2(in_7), .in_3(in_6), .in_4(in_5), .out_5(not_1_out_5[0]), .out_6(not_1_out_5[1]),
    .out_7(not_1_out_5[2]), .out_8(not_1_out_5[3]), .out_9(not_1_out_5[4]), .out_10(not_1_out_5[5]),
    .out_11(not_1_out_5[6]), .out_12(not_1_out_5[7]));
  AND and_1 (.Operand_1({in_5, in_6, in_7, in_8}), .Operand_2({in_1, in_2, in_3, in_4}), .B1(and_1_b1));
  OR or_1 (.Operand_1({in_5, in_6, in_7, in_8}), .Operand_2({in_1, in_2, in_3, in_4}), .B1(or_1_b1));
  MUX_8x1_8Bit mux_8x1_8bit_2 (
    .I2(fullshiftright_1_out_3), .I3(fullshifter_1_out_3), .I4(xor_1_b1), .I5(or_1_b1), .I6(and_1_b1),
    .I7(not_1_out_5), .Iout(mux_8x1_8bit_2_iout), .Sel({in_11, in_10, in_9}));  // open: I0, I1
  XOR xor_1 (.Op_1({in_5, in_6, in_7, in_8}), .Op_2({in_1, in_2, in_3, in_4}), .B1(xor_1_b1));
  FullShifter fullshifter_1 (
    .Operand_1({in_5, in_6, in_7, in_8}), .out_3(fullshifter_1_out_3), .Operand_2({in_1, in_2, in_3, in_4}));
  FullSHiftRight fullshiftright_1 (
    .in_1({in_5, in_6, in_7, in_8}), .out_3(fullshiftright_1_out_3), .in_2({in_1, in_2, in_3, in_4}));

  // Notes on the sheet:
  //   Operand 2
  //   Operand 1
endmodule

module FullCircuit (
  input  in_1,
  input  Operand_2,
  input  in_3,
  input  in_4,
  input  in_5,
  input  in_6,
  input  in_7,
  input  in_8,
  input  in_9,
  input  Operation,
  input  in_11,
  input  in_12
);

  wire [3:0] alu_1_out_13, alu_1_out_13_2;

  Hex_Digit_Display hex_digit_display_1 (.value({in_1, Operand_2, in_3, in_4}));  // open: dp
  Alu alu_1 (
    .in_9(in_9), .in_10(Operation), .in_11(in_11), .in_12(in_12), .out_13({alu_1_out_13_2, alu_1_out_13}),
    .in_1(in_1), .in_2(Operand_2), .in_3(in_3), .in_4(in_4), .in_5(in_5), .in_6(in_6), .in_7(in_7),
    .in_8(in_8));
  Hex_Digit_Display hex_digit_display_2 (.value(alu_1_out_13_2));  // open: dp
  Hex_Digit_Display hex_digit_display_3 (.value(alu_1_out_13));  // open: dp
  Hex_Digit_Display hex_digit_display_4 (.value({in_5, in_6, in_7, in_8}));  // open: dp

  // Notes on the sheet:
  //   Operand 1
  //   0000 -->Move
  //   0001-->Negative
  //   0010-->Add
  //   0011-->Subtract
  //   0100 -->Multiply
  //   1000-->Not
  //   1001-->And
  //   1010-->OR
  //   1011 -->XOR
  //   1100-->Shift left
  //   1101-->Shift right
endmodule
