// Logisim project AND.circ as structural Verilog: 1 circuit, main circuit AND
module AND (
  input  [3:0] Operand_1,
  input  [3:0] Operand_2,
  output [7:0] B1
);

  wire [3:0] and_1_out;

  assign and_1_out = Operand_1 & Operand_2;  // AND_Gate and_1, 4 bits wide
  assign B1 = {{4{1'b0}}, and_1_out};  // Bit_Extender bit_extender_1
endmodule
