// Logisim project FullAdderCirc.circ as structural Verilog: 1 circuit, main circuit FullAdder
// FA
module FullAdder (
  input  A,
  input  B,
  input  C_in,
  output S_out,
  output C_out
);

  wire halfadder_1_carry, halfadder_1_sum, halfadder_2_carry;

  HalfAdder halfadder_1 (.I0(A), .I1(B), .Sum(halfadder_1_sum), .carry(halfadder_1_carry));
  HalfAdder halfadder_2 (.I0(halfadder_1_sum), .I1(C_in), .Sum(S_out), .carry(halfadder_2_carry));
  or or_1 (C_out, halfadder_2_carry, halfadder_1_carry);

  // Notes on the sheet:
  //   S1
  //   C1
  //   S2
  //   C2
endmodule
