// Logisim project HalfAdderCirc.circ as structural Verilog: 1 circuit, main circuit HalfAdder
// HA
module HalfAdder (
  input  I0,
  input  I1,
  output Sum,
  output carry
);

  xor xor_1 (Sum, I0, I1);
  and and_1 (carry, I0, I1);
endmodule
