// Logisim project MUX2x1.circ as structural Verilog: 1 circuit, main circuit MUX2x1
module MUX2x1 (
  input  I0,
  input  I1,
  input  S,
  output out_4
);

  wire and_1_out, and_2_out, not_1_out;

  and and_1 (and_1_out, I0, S);
  and and_2 (and_2_out, I1, not_1_out);
  not not_1 (not_1_out, S);
  or or_1 (out_4, and_1_out, and_2_out);
endmodule
