// Logisim project MUX4x1_8Bit.circ as structural Verilog: 1 circuit, main circuit MUX_4x1_8Bit
// MUX_4x1
module MUX_4x1_8Bit (
  input  [7:0] I0,
  input  [7:0] I1,
  input  [7:0] I2,
  input  [7:0] I3,
  input  [1:0] in_5,
  output [7:0] out_6
);

  wire [7:0] mux_2x1_8bit_1_out_4, mux_2x1_8bit_2_out_4;

  MUX_2x1_8Bit mux_2x1_8bit_1 (.in_1(I0), .in_2(I1), .out_4(mux_2x1_8bit_1_out_4), .in_3(in_5[0]));
  MUX_2x1_8Bit mux_2x1_8bit_2 (.in_1(I2), .in_2(I3), .out_4(mux_2x1_8bit_2_out_4), .in_3(in_5[0]));
  MUX_2x1_8Bit mux_2x1_8bit_3 (.in_1(mux_2x1_8bit_1_out_4), .in_2(mux_2x1_8bit_2_out_4), .out_4(out_6), .in_3(in_5[1]));
endmodule
