// Logisim project MUX8x1_8Bit.circ as structural Verilog: 1 circuit, main circuit MUX_8x1_8Bit
// MUX_8x1
module MUX_8x1_8Bit (
  input  [7:0] I0,
  input  [7:0] I1,
  input  [7:0] I2,
  input  [7:0] I3,
  input  [7:0] I4,
  input  [7:0] I5,
  input  [7:0] I6,
  input  [7:0] I7,
  input  [2:0] Sel,
  output [7:0] Iout
);

  wire [7:0] mux_4x1_8bit_1_out_6, mux_4x1_8bit_2_out_6;

  MUX_4x1_8Bit mux_4x1_8bit_1 (.I0(I0), .I1(I1), .I2(I2), .I3(I3), .out_6(mux_4x1_8bit_1_out_6), .in_5(Sel[1:0]));
  MUX_4x1_8Bit mux_4x1_8bit_2 (.I0(I4), .I1(I5), .I2(I6), .I3(I7), .out_6(mux_4x1_8bit_2_out_6), .in_5(Sel[1:0]));
  MUX_2x1_8Bit mux_2x1_8bit_1 (.in_1(mux_4x1_8bit_1_out_6), .in_2(mux_4x1_8bit_2_out_6), .out_4(Iout), .in_3(Sel[2]));
endmodule
