// Logisim project Move.circ as structural Verilog: 1 circuit, main circuit Move
module Move (
  input  [3:0] in_1,
  output [7:0] out_2
);

  assign out_2 = {{4{1'b0}}, in_1};  // Bit_Extender bit_extender_1
endmodule
