// Logisim project Multiplyer's Adder.circ as structural Verilog: 1 circuit, main circuit Multiplyer's Adder
// 4Bit Adder
module Multiplyer_s_Adder (
  input  A0,
  input  B0,
  input  A1,
  input  B1,
  input  A2,
  input  B2,
  input  A3,
  input  B3,
  output S0,
  output S1,
  output S2,
  output S3,
  output C_out
);

  wire fulladder_1_c_out, fulladder_2_c_out, halfadder_1_carry;

  HalfAdder halfadder_1 (.I0(A0), .I1(B0), .Sum(S0), .carry(halfadder_1_carry));
  FullAdder fulladder_1 (.A(halfadder_1_carry), .B(A1), .C_in(B1), .S_out(S1), .C_out(fulladder_1_c_out));
  FullAdder fulladder_2 (.A(fulladder_1_c_out), .B(A2), .C_in(B2), .S_out(S2), .C_out(fulladder_2_c_out));
  FullAdder fulladder_3 (.A(fulladder_2_c_out), .B(A3), .C_in(B3), .S_out(S3), .C_out(C_out));
endmodule
