// Logisim project Mux_8Bit.circ as structural Verilog: 1 circuit, main circuit MUX_2x1_8Bit
// MUX 2x1
module MUX_2x1_8Bit (
  input  [7:0] in_1,
  input  [7:0] in_2,
  input  in_3,
  output [7:0] out_4
);

  wire not_1_out;
  wire [7:0] and_1_out, and_2_out, bit_extender_1_out, bit_extender_2_out;

  not not_1 (not_1_out, in_3);
  assign bit_extender_1_out = {{7{in_3}}, in_3};  // Bit_Extender bit_extender_1
  assign bit_extender_2_out = {{7{not_1_out}}, not_1_out};  // Bit_Extender bit_extender_2
  assign and_1_out = in_1 & bit_extender_1_out;  // AND_Gate and_1, 8 bits wide
  assign and_2_out = in_2 & bit_extender_2_out;  // AND_Gate and_2, 8 bits wide
  assign out_4 = and_1_out | and_2_out;  // OR_Gate or_1, 8 bits wide
endmodule
