// Logisim project NOT.circ as structural Verilog: 1 circuit, main circuit NOT
module NOT (
  input  in_1,
  input  in_2,
  input  in_3,
  input  in_4,
  output out_5,
  output out_6,
  output out_7,
  output out_8,
  output out_9,
  output out_10,
  output out_11,
  output out_12
);

  not not_1 (out_5, in_1);
  not not_2 (out_6, in_2);
  not not_3 (out_7, in_3);
  not not_4 (out_8, in_4);
  not not_5 (out_9, 1'b0);
  not not_6 (out_10, 1'b0);
  not not_7 (out_11, 1'b0);
  not not_8 (out_12, 1'b0);
endmodule
