// Logisim project Negative.circ as structural Verilog: 1 circuit, main circuit Negative
module Negative (
  input  in_1,
  input  in_2,
  input  in_3,
  input  in_4,
  output out_5,
  output out_6,
  output out_7,
  output out_8,
  output out_9,
  output out_10,
  output out_11,
  output out_12
);

  wire n4bit_adder_1_c_out, not_1_out, not_2_out, not_3_out, not_4_out;
  wire [4:0] n4bit_adder_1_s0;

  not not_1 (not_1_out, in_1);
  not not_2 (not_2_out, in_2);
  not not_3 (not_3_out, in_3);
  not not_4 (not_4_out, in_4);
  _4Bit_Adder u_4bit_adder_1 (
    .Cin(1'b1), .A0(not_1_out), .B0(1'b0), .A1(not_2_out), .B1(1'b0), .A2(not_3_out), .B2(1'b0),
    .A3(not_4_out), .B3(1'b0), .S0(n4bit_adder_1_s0[0]), .S1(n4bit_adder_1_s0[1]), .S2(n4bit_adder_1_s0[2]),
    .S3(n4bit_adder_1_s0[3]), .C_out(n4bit_adder_1_c_out));
  not not_5 (n4bit_adder_1_s0[4], n4bit_adder_1_c_out);
  assign {out_12, out_11, out_10, out_9, out_8, out_7, out_6, out_5} = {{3{n4bit_adder_1_s0[4]}}, n4bit_adder_1_s0};  // Bit_Extender bit_extender_1
endmodule
