// Logisim project OR.circ as structural Verilog: 1 circuit, main circuit OR
module OR (
  input  [3:0] Operand_1,
  input  [3:0] Operand_2,
  output [7:0] B1
);

  wire [3:0] or_1_out;

  assign or_1_out = Operand_1 | Operand_2;  // OR_Gate or_1, 4 bits wide
  assign B1 = {{4{1'b0}}, or_1_out};  // Bit_Extender bit_extender_1
endmodule
