// Logisim project ShiftLeft.circ as structural Verilog: 2 circuits, main circuit ShiftLeft
// Shift-L
module ShiftLeft (
  input  [7:0] in_1,
  output [7:0] Left_7,
  output [7:0] Left_6,
  output [7:0] Left_5,
  output [7:0] Left_4,
  output [7:0] Left_3,
  output [7:0] Left_2,
  output [7:0] Left1,
  output [7:0] Left0
);

  ShiftLeft1 shiftleft1_1 (.in_1(in_1), .out_2(Left1));
  ShiftLeft1 shiftleft1_2 (.in_1(Left1), .out_2(Left_2));
  ShiftLeft1 shiftleft1_3 (.in_1(Left_2), .out_2(Left_3));
  ShiftLeft1 shiftleft1_4 (.in_1(Left_3), .out_2(Left_4));
  ShiftLeft1 shiftleft1_5 (.in_1(Left_4), .out_2(Left_5));
  ShiftLeft1 shiftleft1_6 (.in_1(Left_5), .out_2(Left_6));
  ShiftLeft1 shiftleft1_7 (.in_1(Left_6), .out_2(Left_7));

  assign Left0 = in_1;
endmodule

// Left
module FullShifter (
  input  [3:0] Operand_1,
  input  [3:0] Operand_2,
  output [7:0] out_3
);

  wire [7:0] bit_extender_1_out, bit_extender_2_out, mux_8x1_8bit_1_iout, mux_8x1_8bit_2_iout,
       shiftleft_1_left0, shiftleft_1_left1, shiftleft_1_left_2, shiftleft_1_left_3, shiftleft_1_left_4,
       shiftleft_1_left_5, shiftleft_1_left_6, shiftleft_1_left_7;

  assign bit_extender_1_out = {{4{1'b0}}, Operand_1};  // Bit_Extender bit_extender_1
  assign bit_extender_2_out = {{7{1'b0}}, 1'b0};  // Bit_Extender bit_extender_2
  ShiftLeft shiftleft_1 (
    .in_1(bit_extender_1_out), .Left0(shiftleft_1_left0), .Left1(shiftleft_1_left1),
    .Left_2(shiftleft_1_left_2), .Left_3(shiftleft_1_left_3), .Left_4(shiftleft_1_left_4),
    .Left_5(shiftleft_1_left_5), .Left_6(shiftleft_1_left_6), .Left_7(shiftleft_1_left_7));
  MUX_8x1_8Bit mux_8x1_8bit_1 (
    .I0(bit_extender_2_out), .I1(bit_extender_2_out), .I2(bit_extender_2_out), .I3(bit_extender_2_out),
    .I4(bit_extender_2_out), .I5(bit_extender_2_out), .I6(bit_extender_2_out), .I7(bit_extender_2_out),
    .Iout(mux_8x1_8bit_1_iout));  // open: Sel
  MUX_8x1_8Bit mux_8x1_8bit_2 (
    .I0(shiftleft_1_left_7), .I1(shiftleft_1_left_6), .I2(shiftleft_1_left_5), .I3(shiftleft_1_left_4),
    .I4(shiftleft_1_left_3), .I5(shiftleft_1_left_2), .I6(shiftleft_1_left1), .I7(shiftleft_1_left0),
    .Iout(mux_8x1_8bit_2_iout), .Sel(Operand_2[2:0]));
  MUX_2x1_8Bit mux_2x1_8bit_1 (
    .in_1(mux_8x1_8bit_1_iout), .in_2(mux_8x1_8bit_2_iout), .out_4(out_3), .in_3(Operand_2[3]));
endmodule
