// Logisim project ShiftLeft1.circ as structural Verilog: 1 circuit, main circuit ShiftLeft1
// Left-1
module ShiftLeft1 (
  input  [7:0] in_1,
  output [7:0] out_2
);


  assign out_2 = {in_1[6:0], 1'b0};
endmodule
