// Logisim project ShiftRight.circ as structural Verilog: 2 circuits, main circuit Shift Right
module Shift_Right (
  input  [7:0] in_1,
  output [7:0] Shift_Right_4,
  output [7:0] Shift_Right_3,
  output [7:0] Shift_Right_2,
  output [7:0] Shift_Right_1,
  output [7:0] Shift_Right_0
);

  ShiftRight1 shiftright1_1 (.in_1(in_1), .Shift_Right_1(Shift_Right_1));
  ShiftRight1 shiftright1_2 (.in_1(Shift_Right_1), .Shift_Right_1(Shift_Right_2));
  ShiftRight1 shiftright1_3 (.in_1(Shift_Right_2), .Shift_Right_1(Shift_Right_3));
  ShiftRight1 shiftright1_4 (.in_1(Shift_Right_3), .Shift_Right_1(Shift_Right_4));

  assign Shift_Right_0 = in_1;
endmodule

// Right
module FullSHiftRight (
  input  [3:0] in_1,
  input  [3:0] in_2,
  output [7:0] out_3
);

  wire [7:0] bit_extender_1_out, bit_extender_2_out, mux_8x1_8bit_1_iout, mux_8x1_8bit_2_iout,
       shift_right_1_shift_right_0, shift_right_1_shift_right_1, shift_right_1_shift_right_2,
       shift_right_1_shift_right_3, shift_right_1_shift_right_4;

  assign bit_extender_1_out = {{4{1'b0}}, in_1};  // Bit_Extender bit_extender_1
  Shift_Right shift_right_1 (
    .in_1(bit_extender_1_out), .Shift_Right_4(shift_right_1_shift_right_4),
    .Shift_Right_3(shift_right_1_shift_right_3), .Shift_Right_2(shift_right_1_shift_right_2),
    .Shift_Right_1(shift_right_1_shift_right_1), .Shift_Right_0(shift_right_1_shift_right_0));
  assign bit_extender_2_out = {{7{1'b0}}, 1'b0};  // Bit_Extender bit_extender_2
  MUX_8x1_8Bit mux_8x1_8bit_1 (
    .I0(bit_extender_2_out), .I1(bit_extender_2_out), .I2(bit_extender_2_out), .I3(bit_extender_2_out),
    .I4(bit_extender_2_out), .I5(bit_extender_2_out), .I6(bit_extender_2_out), .I7(bit_extender_2_out),
    .Iout(mux_8x1_8bit_1_iout));  // open: Sel
  MUX_8x1_8Bit mux_8x1_8bit_2 (
    .I0(bit_extender_2_out), .I1(bit_extender_2_out), .I2(bit_extender_2_out),
    .I3(shift_right_1_shift_right_4), .I4(shift_right_1_shift_right_3), .I5(shift_right_1_shift_right_2),
    .I6(shift_right_1_shift_right_1), .I7(shift_right_1_shift_right_0), .Iout(mux_8x1_8bit_2_iout),
    .Sel(in_2[2:0]));
  MUX_2x1_8Bit mux_2x1_8bit_1 (.in_1(mux_8x1_8bit_1_iout), .in_2(mux_8x1_8bit_2_iout), .out_4(out_3), .in_3(in_2[3]));
endmodule
