// Logisim project ShiftRight1.circ as structural Verilog: 1 circuit, main circuit ShiftRight1
// right1
module ShiftRight1 (
  input  [7:0] in_1,
  output [7:0] Shift_Right_1
);


  assign Shift_Right_1 = {1'b0, in_1[7:1]};
endmodule
