// Logisim project Shifter.circ as structural Verilog: 18 circuits, main circuit Left 0
module Left_0 (
  input  [3:0] in_1,
  output [7:0] out_2
);


  assign out_2 = {4'b0000, in_1};
endmodule

module Left_1 (
  input  [3:0] in_1,
  output [7:0] out_2
);


  assign out_2 = {3'b000, in_1, 1'b0};
endmodule

module Left_2 (
  input  [3:0] in_1,
  output [7:0] out_2
);


  assign out_2 = {2'b00, in_1, 2'b00};
endmodule

module Left_3 (
  input  [3:0] in_1,
  output [7:0] out_2
);


  assign out_2 = {1'b0, in_1, 3'b000};
endmodule

module Left_4 (
  input  [3:0] in_1,
  output [7:0] out_2
);


  assign out_2 = {in_1, 4'b0000};
endmodule

module Left_5 (
  input  [3:0] in_1,
  output [7:0] out_2
);


  assign out_2 = {in_1[2:0], {5{1'b0}}};
endmodule

module Left_6 (
  input  [3:0] in_1,
  output [7:0] out_2
);


  assign out_2 = {in_1[1:0], {6{1'b0}}};
endmodule

module Left_7 (
  input  [3:0] in_1,
  output [7:0] out_2
);


  assign out_2 = {in_1[0], {7{1'b0}}};
endmodule

module Left_8 (
  input  [3:0] in_1,
  output [7:0] out_2
);


  assign out_2 = {8{1'b0}};
endmodule

module Right_0 (
  input  [3:0] in_1,
  output [7:0] out_2
);


  assign out_2 = {4'b0000, in_1};
endmodule

module Right_1 (
  input  [3:0] in_1,
  output [7:0] out_2
);


  assign out_2 = {{5{1'b0}}, in_1[3:1]};
endmodule

module Right_2 (
  input  [3:0] in_1,
  output [7:0] out_2
);


  assign out_2 = {{6{1'b0}}, in_1[3:2]};
endmodule

module Right_3 (
  input  [3:0] in_1,
  output [7:0] out_2
);


  assign out_2 = {{7{1'b0}}, in_1[3]};
endmodule

module Right_4 (
  input  [3:0] in_1,
  output [7:0] out_2
);


  assign out_2 = {8{1'b0}};
endmodule

module Right_5 (
  input  [3:0] in_1,
  output [7:0] out_2
);


  assign out_2 = {8{1'b0}};
endmodule

module Right_6 (
  input  [3:0] in_1,
  output [7:0] out_2
);


  assign out_2 = {8{1'b0}};
endmodule

module Right_7 (
  input  [3:0] in_1,
  output [7:0] out_2
);


  assign out_2 = {8{1'b0}};
endmodule

module Right_8 (
  input  [3:0] in_1,
  output [7:0] out_2
);


  assign out_2 = {8{1'b0}};
endmodule
