// Logisim project Subtractor.circ as structural Verilog: 1 circuit, main circuit Subtractor
module Subtractor (
  input  A0,
  input  A1,
  input  A2,
  input  A3,
  input  B0,
  input  B1,
  input  B2,
  input  B3,
  output out_9,
  output out_10,
  output out_11,
  output out_12,
  output out_13,
  output out_14,
  output out_15,
  output out_16
);

  wire n4bit_adder_1_c_out, not_1_out, not_2_out, not_3_out, not_4_out;
  wire [4:0] n4bit_adder_1_s0;

  not not_1 (not_1_out, B0);
  not not_2 (not_2_out, B1);
  not not_3 (not_3_out, B2);
  not not_4 (not_4_out, B3);
  _4Bit_Adder u_4bit_adder_1 (
    .Cin(1'b1), .A0(A0), .B0(not_1_out), .A1(A1), .B1(not_2_out), .A2(A2), .B2(not_3_out), .A3(A3),
    .B3(not_4_out), .S0(n4bit_adder_1_s0[0]), .S1(n4bit_adder_1_s0[1]), .S2(n4bit_adder_1_s0[2]),
    .S3(n4bit_adder_1_s0[3]), .C_out(n4bit_adder_1_c_out));
  not not_5 (n4bit_adder_1_s0[4], n4bit_adder_1_c_out);
  assign {out_16, out_15, out_14, out_13, out_12, out_11, out_10, out_9} = {{3{n4bit_adder_1_s0[4]}}, n4bit_adder_1_s0};  // Bit_Extender bit_extender_1

  // Notes on the sheet:
  //   Cin
endmodule
