// Logisim project XOR.circ as structural Verilog: 1 circuit, main circuit XOR
module XOR (
  input  [3:0] Op_1,
  input  [3:0] Op_2,
  output [7:0] B1
);

  wire [3:0] xor_1_out;

  assign xor_1_out = Op_1 ^ Op_2;  // XOR_Gate xor_1, 4 bits wide
  assign B1 = {{4{1'b0}}, xor_1_out};  // Bit_Extender bit_extender_1
endmodule
